# Fritzing sketch 3Leds (saved by Fritzing 0.9.2b)
circuit board: 8.46667cm x 5.64444cm
breadboards: 1

parts:
  Raspberry_Pi1 = Raspberry Pi 2
  R1 = Resistor [tolerance=±5% resistance=220 package=THT]
  R2 = Resistor [tolerance=±5% resistance=220 package=THT]
  LED1 = LED - 5mm [color="Red (633nm)" package="5 mm [THT]"]
  LED2 = LED - 5mm [color="Red (633nm)" package="5 mm [THT]"]
  LED3 = LED - 5mm [color="Red (633nm)" package="5 mm [THT]"]
  R3 = Resistor [tolerance=±5% resistance=220 package=THT]

nets:
  N1: Raspberry_Pi1.3v3, R1.Pin_1, R2.Pin_1, R3.Pin_0
  N2: Raspberry_Pi1.GPIO5, LED1.anode
  N3: Raspberry_Pi1.GPIO6, LED2.anode
  N4: Raspberry_Pi1.GPIO26, LED3.anode
  N5: R1.Pin_0, LED1.cathode
  N6: R2.Pin_0, LED2.cathode
  N7: LED3.cathode, R3.Pin_1
